// Logisim project decoder_4_to_16.circ as structural Verilog: 1 circuit, main circuit decode
module decode (
  input  [3:0] inp,
  input  ie,
  input  vcc,
  input  gnd,
  output x0,
  output x1,
  output x2,
  output x3,
  output x4,
  output x5,
  output x6,
  output x7,
  output x8,
  output x9,
  output xa,
  output xb,
  output xc,
  output xd,
  output xe,
  output xf
);

  wire not_1_out, not_2_out, not_3_out, not_4_out;
  wire [3:0] controlled_buffer_1_out;

  assign controlled_buffer_1_out = ie ? inp : 4'bz;  // Controlled_Buffer controlled_buffer_1
  // NoConnect on vcc
  // NoConnect on gnd
  not not_1 (not_1_out, controlled_buffer_1_out[0]);
  not not_2 (not_2_out, controlled_buffer_1_out[1]);
  not not_3 (not_3_out, controlled_buffer_1_out[2]);
  not not_4 (not_4_out, controlled_buffer_1_out[3]);
  and and_1 (x0, not_1_out, not_2_out, not_3_out, not_4_out);
  and and_2 (x1, controlled_buffer_1_out[0], not_2_out, not_3_out, not_4_out);
  and and_3 (x2, not_1_out, controlled_buffer_1_out[1], not_3_out, not_4_out);
  and and_4 (x3, controlled_buffer_1_out[0], controlled_buffer_1_out[1], not_3_out, not_4_out);
  and and_5 (x4, not_1_out, not_2_out, controlled_buffer_1_out[2], not_4_out);
  and and_6 (x5, controlled_buffer_1_out[0], not_2_out, controlled_buffer_1_out[2], not_4_out);
  and and_7 (x6, not_1_out, controlled_buffer_1_out[1], controlled_buffer_1_out[2], not_4_out);
  and and_8 (x7, controlled_buffer_1_out[0], controlled_buffer_1_out[1], controlled_buffer_1_out[2], not_4_out);
  and and_9 (x8, not_1_out, not_2_out, not_3_out, controlled_buffer_1_out[3]);
  and and_10 (x9, controlled_buffer_1_out[0], not_2_out, not_3_out, controlled_buffer_1_out[3]);
  and and_11 (xa, not_1_out, controlled_buffer_1_out[1], not_3_out, controlled_buffer_1_out[3]);
  and and_12 (xc, not_1_out, not_2_out, controlled_buffer_1_out[2], controlled_buffer_1_out[3]);
  and and_13 (xb, controlled_buffer_1_out[0], controlled_buffer_1_out[1], not_3_out, controlled_buffer_1_out[3]);
  and and_14 (xd, controlled_buffer_1_out[0], not_2_out, controlled_buffer_1_out[2], controlled_buffer_1_out[3]);
  and and_15 (xe, not_1_out, controlled_buffer_1_out[1], controlled_buffer_1_out[2], controlled_buffer_1_out[3]);
  and and_16 (xf, controlled_buffer_1_out[0], controlled_buffer_1_out[1], controlled_buffer_1_out[2], controlled_buffer_1_out[3]);
endmodule
